# Fritzing sketch Soil sensor circuit (saved by Fritzing 0.8.7b)
breadboards: 1
stripboards: 1

parts:
  U2 = LCD-16X2 [package=lcd-16x2]
  R1 = TRIMPOT [package=3362u-2]
  Q1 = TRANSISTOR_PNP [package=to-92]
  U3 = LM358 [package=dip08]
  D1 = Diode [package=diode-1n4148]
  Part1 = Arduino Uno (Rev3)
  M1 = DC Motor
  R3 = Resistor [tolerance=±5% resistance=3.3k package=THT]
  R4 = Resistor [tolerance=±5% resistance=330 package=THT]
  R6 = Resistor [tolerance=±5% resistance=2.2k package=THT]
  R7 = Resistor [tolerance=±5% resistance=100 package=THT]
  R8 = Resistor [tolerance=±5% resistance=100 package=THT]
  Q2 = NPN-Transistor [package="TO92 [THT]"]

nets:
  VSS: U2.VSS, U2.R_W, U2.K, R1.CCW, Q1.C, U3.G$1_V-, Part1.GND, R3.Pin_0, R8.Pin_1
  VDD: U2.VDD, U2.A, R1.CW, U3.G$1_V+, D1.C, Part1.5V, M1.pin_1, R7.Pin_1, Q2.C
  N1: U2.VO, R3.Pin_1
  N2: U2.RS, Part1.D12/MISO
  N3: U2.E, Part1.D11_PWM/MOSI
  N4: U2.DB4, Part1.D5_PWM
  N5: U2.DB5, Part1.D4
  N6: U2.DB6, Part1.D3_PWM
  N7: U2.DB7, Part1.D2
  N8: R1.WIPER, U3.G$1_+IN, R6.Pin_0
  N9: Q1.E, D1.A, M1.pin_2
  N10: Q1.B, R4.Pin_1
  N11: U3.G$1_OUT, R4.Pin_0, R6.Pin_1
  N12: U3.G$1_-IN, Part1.A0, R8.Pin_0, Q2.E

notes:
  Here I am using an ArduinoUno in place of a Sparkfun RedBoard.
  This protoboard is the soil sensor with the purple and yellow wires going to metal rods in the soil.
